// Logisim project 12 BIT.circ as structural Verilog: 1 circuit, main circuit main
module main (
  input  CLK,
  input  CLR,
  input  LOAD,
  input  INCR,
  input  [15:0] INPUT,
  output [15:0] OUTPUT
);

  _12_BIT_register_main main_1 (
    .CLK(CLK), .Clear(CLR), .Load(LOAD), .Increment(INCR), .I1(INPUT[0]), .I2(INPUT[1]), .I3(INPUT[2]),
    .I4(INPUT[3]), .I5(INPUT[4]), .I6(INPUT[5]), .I7(INPUT[6]), .I8(INPUT[7]), .I9(INPUT[8]), .I10(INPUT[9]),
    .I11(INPUT[10]), .I12(INPUT[11]), .A1(OUTPUT[0]), .A2(OUTPUT[1]), .A3(OUTPUT[2]), .A4(OUTPUT[3]),
    .A5(OUTPUT[4]), .A6(OUTPUT[5]), .A7(OUTPUT[6]), .A8(OUTPUT[7]), .A9(OUTPUT[8]), .A10(OUTPUT[9]),
    .A11(OUTPUT[10]), .A12(OUTPUT[11]));

  assign OUTPUT[15:12] = 4'b0000;
endmodule
