// Logisim project 12BIT FOR RESI.circ as structural Verilog: 1 circuit, main circuit main
module main (
  input  LOAD,
  input  [11:0] INPUT,
  input  CLK,
  output [11:0] out_4
);

  D_Flip_Flop d_ff_1 (.clk(CLK), .D(INPUT[0]), .Q(out_4[0]), .en(LOAD));  // open: Qn, preset, reset
  D_Flip_Flop d_ff_2 (.clk(CLK), .D(INPUT[1]), .Q(out_4[1]), .en(LOAD));  // open: Qn, preset, reset
  D_Flip_Flop d_ff_3 (.clk(CLK), .D(INPUT[2]), .Q(out_4[2]), .en(LOAD));  // open: Qn, preset, reset
  D_Flip_Flop d_ff_4 (.clk(CLK), .D(INPUT[3]), .Q(out_4[3]), .en(LOAD));  // open: Qn, preset, reset
  D_Flip_Flop d_ff_5 (.clk(CLK), .D(INPUT[4]), .Q(out_4[4]), .en(LOAD));  // open: Qn, preset, reset
  D_Flip_Flop d_ff_6 (.clk(CLK), .D(INPUT[5]), .Q(out_4[5]), .en(LOAD));  // open: Qn, preset, reset
  D_Flip_Flop d_ff_7 (.clk(CLK), .D(INPUT[6]), .Q(out_4[6]), .en(LOAD));  // open: Qn, preset, reset
  D_Flip_Flop d_ff_8 (.clk(CLK), .D(INPUT[7]), .Q(out_4[7]), .en(LOAD));  // open: Qn, preset, reset
  D_Flip_Flop d_ff_9 (.clk(CLK), .D(INPUT[8]), .Q(out_4[8]), .en(LOAD));  // open: Qn, preset, reset
  D_Flip_Flop d_ff_10 (.clk(CLK), .D(INPUT[9]), .Q(out_4[9]), .en(LOAD));  // open: Qn, preset, reset
  D_Flip_Flop d_ff_11 (.clk(CLK), .D(INPUT[10]), .Q(out_4[10]), .en(LOAD));  // open: Qn, preset, reset
  D_Flip_Flop d_ff_12 (.clk(CLK), .D(INPUT[11]), .Q(out_4[11]), .en(LOAD));  // open: Qn, preset, reset
endmodule
