// Logisim project 3BIT RESIS.circ as structural Verilog: 1 circuit, main circuit main
module main (
  input  LD,
  input  D1,
  input  D2,
  input  D3,
  input  CLK,
  output [2:0] OUTPUT
);

  D_Flip_Flop d_ff_1 (.clk(CLK), .D(D1), .Q(OUTPUT[0]), .en(LD));  // open: Qn, preset, reset
  D_Flip_Flop d_ff_2 (.clk(CLK), .D(D2), .Q(OUTPUT[1]), .en(LD));  // open: Qn, preset, reset
  D_Flip_Flop d_ff_3 (.clk(CLK), .D(D3), .Q(OUTPUT[2]), .en(LD));  // open: Qn, preset, reset
endmodule
