// Logisim project 3CROSS8 DECODDER .circ as structural Verilog: 1 circuit, main circuit main
module main (
  input  A,
  input  B,
  input  C,
  output D0,
  output D1,
  output D2,
  output D3,
  output D4,
  output D5,
  output D6,
  output D7
);

  wire not_1_out, not_2_out, not_3_out;

  not not_1 (not_1_out, A);
  not not_2 (not_2_out, B);
  not not_3 (not_3_out, C);
  and and_1 (D0, not_1_out, not_2_out, not_3_out);
  and and_2 (D1, not_1_out, not_2_out, C);
  and and_3 (D2, not_1_out, B, not_3_out);
  and and_4 (D3, not_1_out, B, C);
  and and_5 (D4, A, not_2_out, not_3_out);
  and and_6 (D5, A, not_2_out, C);
  and and_7 (D6, A, B, not_3_out);
  and and_8 (D7, A, B, C);
endmodule
