// Logisim project 8 BIT register.circ as structural Verilog: 1 circuit, main circuit main
// A16
module main (
  input  CLK,
  input  Clear,
  input  Load,
  input  Increment,
  input  I1,
  input  I2,
  input  I3,
  input  I4,
  input  I5,
  input  I6,
  input  I7,
  input  I8,
  output A1,
  output A2,
  output A3,
  output A4,
  output A5,
  output A6,
  output A7,
  output A8
);

  wire and_1_out, and_2_out, and_3_out, and_4_out, and_5_out, and_6_out, and_7_out, and_8_out, and_9_out,
       and_10_out, and_11_out, and_12_out, and_13_out, and_14_out, and_15_out, and_16_out, and_17_out,
       and_18_out, and_19_out, and_20_out, and_21_out, and_22_out, and_23_out, and_24_out, and_25_out,
       not_1_out, not_2_out, not_3_out, not_4_out, not_5_out, not_6_out, not_7_out, not_8_out, not_9_out,
       not_10_out, or_1_out, or_2_out, or_3_out, or_4_out, or_5_out, or_6_out, or_7_out, or_8_out, or_9_out,
       or_10_out, or_11_out, or_12_out, or_13_out, or_14_out, or_15_out, or_16_out;

  not not_1 (not_1_out, Clear);
  not not_2 (not_2_out, Load);
  not not_3 (not_3_out, I1);
  not not_4 (not_4_out, I2);
  not not_5 (not_5_out, I3);
  not not_6 (not_6_out, I4);
  not not_7 (not_7_out, I5);
  not not_8 (not_8_out, I6);
  not not_9 (not_9_out, I7);
  not not_10 (not_10_out, I8);
  and and_1 (and_1_out, not_1_out, Load);
  and and_2 (and_2_out, not_1_out, not_2_out, Increment);
  and and_3 (and_3_out, and_1_out, I1);
  and and_4 (and_4_out, and_1_out, not_3_out);
  and and_5 (and_5_out, and_2_out, A1);
  and and_6 (and_6_out, and_1_out, I2);
  and and_7 (and_7_out, and_1_out, not_4_out);
  and and_8 (and_8_out, and_5_out, A2);
  and and_9 (and_9_out, and_1_out, I3);
  and and_10 (and_10_out, and_1_out, not_5_out);
  and and_11 (and_11_out, and_1_out, I4);
  and and_12 (and_12_out, and_1_out, not_6_out);
  and and_13 (and_13_out, and_1_out, I5);
  and and_14 (and_14_out, and_1_out, not_7_out);
  and and_15 (and_15_out, and_1_out, I6);
  and and_16 (and_16_out, and_1_out, not_8_out);
  and and_17 (and_17_out, and_1_out, I7);
  and and_18 (and_18_out, and_1_out, not_9_out);
  and and_19 (and_19_out, and_1_out, I8);
  and and_20 (and_20_out, and_1_out, not_10_out);
  and and_21 (and_21_out, and_8_out, A3);
  and and_22 (and_22_out, and_21_out, A4);
  and and_23 (and_23_out, and_22_out, A5);
  and and_24 (and_24_out, and_23_out, A6);
  and and_25 (and_25_out, and_24_out, A7);
  or or_1 (or_1_out, and_2_out, and_3_out);
  or or_2 (or_2_out, Clear, and_2_out, and_4_out);
  or or_3 (or_3_out, and_5_out, and_6_out);
  or or_4 (or_4_out, Clear, and_5_out, and_7_out);
  or or_5 (or_5_out, and_8_out, and_9_out);
  or or_6 (or_6_out, Clear, and_8_out, and_10_out);
  or or_7 (or_7_out, and_21_out, and_11_out);
  or or_8 (or_8_out, Clear, and_21_out, and_12_out);
  or or_9 (or_9_out, and_22_out, and_13_out);
  or or_10 (or_10_out, Clear, and_22_out, and_14_out);
  or or_11 (or_11_out, and_23_out, and_15_out);
  or or_12 (or_12_out, Clear, and_23_out, and_16_out);
  or or_13 (or_13_out, and_24_out, and_17_out);
  or or_14 (or_14_out, Clear, and_24_out, and_18_out);
  or or_15 (or_15_out, and_25_out, and_19_out);
  or or_16 (or_16_out, Clear, and_25_out, and_20_out);
  J_K_Flip_Flop j_k_ff_1 (.J(or_1_out), .clk(CLK), .K(or_2_out), .Q(A1));  // open: Qn, preset, en, reset
  J_K_Flip_Flop j_k_ff_2 (.J(or_3_out), .clk(CLK), .K(or_4_out), .Q(A2));  // open: Qn, preset, en, reset
  J_K_Flip_Flop j_k_ff_3 (.J(or_5_out), .clk(CLK), .K(or_6_out), .Q(A3));  // open: Qn, preset, en, reset
  J_K_Flip_Flop j_k_ff_4 (.J(or_7_out), .clk(CLK), .K(or_8_out), .Q(A4));  // open: Qn, preset, en, reset
  J_K_Flip_Flop j_k_ff_5 (.J(or_9_out), .clk(CLK), .K(or_10_out), .Q(A5));  // open: Qn, preset, en, reset
  J_K_Flip_Flop j_k_ff_6 (.J(or_11_out), .clk(CLK), .K(or_12_out), .Q(A6));  // open: Qn, preset, en, reset
  J_K_Flip_Flop j_k_ff_7 (.J(or_13_out), .clk(CLK), .K(or_14_out), .Q(A7));  // open: Qn, preset, en, reset
  J_K_Flip_Flop j_k_ff_8 (.J(or_15_out), .clk(CLK), .K(or_16_out), .Q(A8));  // open: Qn, preset, en, reset
endmodule
