// Logisim project 8 BIT.circ as structural Verilog: 1 circuit, main circuit main
module main (
  input  CLK,
  input  CLR,
  input  LOAD,
  input  INCR,
  input  [15:0] INPUT,
  output [15:0] OUTPUT
);

  _8_BIT_register_main main_1 (
    .CLK(CLK), .Clear(CLR), .Load(LOAD), .Increment(INCR), .I1(INPUT[0]), .I2(INPUT[1]), .I3(INPUT[2]),
    .I4(INPUT[3]), .I5(INPUT[4]), .I6(INPUT[5]), .I7(INPUT[6]), .I8(INPUT[7]), .A1(OUTPUT[0]),
    .A2(OUTPUT[1]), .A3(OUTPUT[2]), .A4(OUTPUT[3]), .A5(OUTPUT[4]), .A6(OUTPUT[5]), .A7(OUTPUT[6]),
    .A8(OUTPUT[7]));

  assign OUTPUT[15:8] = {8{1'b0}};
endmodule
