// Logisim project ALU 0 BIT.circ as structural Verilog: 1 circuit, main circuit main
module main (
  input  AND,
  input  AC,
  input  DR,
  input  ADD,
  input  DDR,
  input  DINPR,
  input  INPR,
  input  COM,
  input  SHR,
  input  AC_N,
  input  SHL,
  input  E,
  output S,
  output AC_2,
  output E_2
);

  wire and_1_out, and_2_out, and_3_out, and_4_out, and_5_out, and_6_out, and_8_out, main_1_p4, not_1_out;

  not not_1 (not_1_out, AC);
  and and_1 (and_1_out, AC, DR);
  // HA_main main_1: pin names not known; wires that end beside it: AC, DR, S, main_1_p4
  and and_2 (and_2_out, AND, and_1_out);
  and and_3 (and_3_out, ADD, main_1_p4);
  and and_4 (and_4_out, DDR, DR);
  and and_5 (and_5_out, DINPR, INPR);
  buf and_6 (and_6_out, COM);  // AND_Gate
  and and_7 (E_2, SHR, AC_N);
  and and_8 (and_8_out, SHL, E);
  or or_1 (AC_2, and_2_out, and_3_out, and_4_out, and_6_out, and_5_out, and_8_out);
endmodule
