// Logisim project ALU.circ as structural Verilog: 1 circuit, main circuit main
module main (
  input  [15:0] INPR,
  input  [15:0] AC,
  input  E,
  input  [15:0] DR,
  input  COM_E,
  input  SHL,
  input  SHR,
  input  DINPR,
  input  COM_AC,
  input  DDR,
  input  ADD,
  input  AND,
  output [15:0] OUT_AC,
  output E_2
);

  CONTROL_main main_1 (
    .AND(AND), .ADD(ADD), .DDR(DDR), .COM_AC(COM_AC), .DINPR(DINPR), .SHR(SHR), .SHL(SHL), .COM_E(COM_E),
    .AC_15(AC[15]), .DR_15(DR[15]), .E(E), .AC_14(AC[14]), .DR_14(DR[14]), .AC_13(AC[13]), .DR_13(DR[13]),
    .AC_12(AC[12]), .DR_12(DR[12]), .AC_11(AC[11]), .DR_11(DR[11]), .AC_10(AC[10]), .DR_10(DR[10]),
    .AC_9(AC[9]), .DR_9(DR[9]), .AC_8(AC[8]), .DR_8(DR[8]), .AC_7(AC[7]), .DR_7(DR[7]), .INPR_7(INPR[7]),
    .AC_6(AC[6]), .DR_6(DR[6]), .INPR_6(INPR[6]), .AC_5(AC[5]), .DR_5(DR[5]), .INPR_5(INPR[5]), .AC_4(AC[4]),
    .DR_4(DR[4]), .INPR_4(INPR[4]), .AC_3(AC[3]), .DR_3(DR[3]), .INPR_3(INPR[3]), .AC_2(AC[2]), .DR_2(DR[2]),
    .INPR_2(INPR[2]), .AC_1(AC[1]), .DR_1(DR[1]), .INPR_1(INPR[1]), .AC_0(AC[0]), .DR_0(DR[0]),
    .INPR_0(INPR[0]), .E_2(E_2), .AC_15_2(OUT_AC[15]), .AC_14_2(OUT_AC[14]), .AC_13_2(OUT_AC[13]),
    .AC_12_2(OUT_AC[12]), .AC_11_2(OUT_AC[11]), .AC_10_2(OUT_AC[10]), .AC_9_2(OUT_AC[9]), .AC_8_2(OUT_AC[8]),
    .AC_7_2(OUT_AC[7]), .AC_6_2(OUT_AC[6]), .AC_5_2(OUT_AC[5]), .AC_4_2(OUT_AC[4]), .AC_3_2(OUT_AC[3]),
    .AC_2_2(OUT_AC[2]), .AC_1_2(OUT_AC[1]), .AC_0_2(OUT_AC[0]));
endmodule
