// Logisim project COMP.circ as structural Verilog: 1 circuit, main circuit main
module main (
  input  in_1,
  input  in_2,
  output [15:0] out_3,
  output [15:0] out_4,
  output [15:0] out_5
);

  wire AC_p7, AC_p8, and_1_out, clock_1_out, DR_dr, E_q, FGI_q, FGO_q, I_q, IEN_q, keyboard_1_avail,
       main_2_i, main_3_add, main_3_and, main_3_clr_ac, main_3_clr_ar, main_3_clr_e, main_3_clr_pc,
       main_3_com_ac, main_3_com_e, main_3_ddr, main_3_dinpr, main_3_fgi_reset, main_3_fgo_reset,
       main_3_incr_ac, main_3_incr_ar, main_3_incr_dr, main_3_incr_pc, main_3_ld_ac, main_3_ld_ar,
       main_3_ld_dr, main_3_ld_e, main_3_ld_ir, main_3_ld_outr, main_3_ld_pc, main_3_ld_tr, main_3_load_i,
       main_3_memory_write, main_3_reset_ien, main_3_reset_r, main_3_reset_s, main_3_sc_reset,
       main_3_set_ien, main_3_set_r, main_3_shl, main_3_shr, main_4_e_2, not_1_out, or_1_out, or_2_out, R_q,
       S_q;
  wire [2:0] main_3_s0;
  wire [3:0] main_1_a1;
  wire [6:0] bit_extender_2_out, decoder_1_out0, keyboard_1_data;
  wire [7:0] main_2_output;
  wire [11:0] bit_extender_1_out, main_2_ir_0_11;
  wire [15:0] AR_output, bit_extender_3_out, DR_output, IR_output, main_4_out_ac, multiplexer_1_out,
       PC_output, ram_1_data, TR_output;

  Clock clock_1 (.out(clock_1_out));
  COUNTER_main main_1 (.CLK(clock_1_out), .Clear(main_3_sc_reset), .Load(S_q), .A1(main_1_a1));
  Decoder #(.select(4), .enable("false")) decoder_1 (
    .out0(decoder_1_out0[0]), .out1(decoder_1_out0[1]), .out2(decoder_1_out0[2]), .out3(decoder_1_out0[3]),
    .out4(decoder_1_out0[4]), .out5(decoder_1_out0[5]), .out6(decoder_1_out0[6]), .sel(main_1_a1));  // open: out7, out8, out9, out10, out11, out12, out13, out14, out15
  IR_CONTROL_main main_2 (.IR_INPUT(IR_output), .IR_0_11(main_2_ir_0_11), .OUTPUT(main_2_output), .I(main_2_i));
  D_Flip_Flop I (.clk(clock_1_out), .D(main_2_i), .Q(I_q), .en(main_3_load_i));  // open: Qn, preset, reset
  and and_1 (and_1_out, main_3_s0[0], main_3_s0[1], main_3_s0[2]);
  CU_main main_3 (
    .R(R_q), .TIME(decoder_1_out0), .DECODED__BIT(main_2_output), .IEN(IEN_q), .IR_0_11(main_2_ir_0_11),
    .I(I_q), .DR(DR_dr), .FGO(FGO_q), .FGI(FGI_q), .E(E_q), .AC(AC_p8), .AC_15(AC_p7), .S0(main_3_s0[0]),
    .S1(main_3_s0[1]), .S2(main_3_s0[2]), .COM_E(main_3_com_e), .AND(main_3_and), .ADD(main_3_add),
    .DDR(main_3_ddr), .DINPR(main_3_dinpr), .COM_AC(main_3_com_ac), .SHR(main_3_shr), .SHL(main_3_shl),
    .SET_R(main_3_set_r), .LD_AR(main_3_ld_ar), .LOAD_I(main_3_load_i), .LD_PC(main_3_ld_pc),
    .SET_IEN(main_3_set_ien), .LD_DR(main_3_ld_dr), .LD_AC(main_3_ld_ac), .LD_E(main_3_ld_e),
    .LD_IR(main_3_ld_ir), .LD_TR(main_3_ld_tr), .LD_OUTR(main_3_ld_outr), .CLR_AR(main_3_clr_ar),
    .CLR_E(main_3_clr_e), .CLR_PC(main_3_clr_pc), .CLR_AC(main_3_clr_ac), .RESET_IEN(main_3_reset_ien),
    .RESET_R(main_3_reset_r), .SC_RESET(main_3_sc_reset), .INCR_AR(main_3_incr_ar),
    .FGI_RESET(main_3_fgi_reset), .INCR_PC(main_3_incr_pc), .INCR_DR(main_3_incr_dr),
    .INCR_AC(main_3_incr_ac), .MEMORY_WRITE(main_3_memory_write), .RESET_S(main_3_reset_s),
    .FGO_RESET(main_3_fgo_reset));
  J_K_Flip_Flop R (.J(main_3_set_r), .clk(clock_1_out), .K(main_3_reset_r), .Q(R_q));  // open: Qn, preset, en, reset
  ALU_main main_4 (
    .OUT_AC(main_4_out_ac), .E_2(main_4_e_2), .INPR(out_4), .AC(out_3), .E(E_q), .DR(DR_output),
    .COM_E(main_3_com_e), .SHL(main_3_shl), .SHR(main_3_shr), .DINPR(main_3_dinpr), .COM_AC(main_3_com_ac),
    .DDR(main_3_ddr), .ADD(main_3_add), .AND(main_3_and));
  D_Flip_Flop E (
    .clk(clock_1_out), .D(main_4_e_2), .Q(E_q), .en(main_3_ld_e), .reset(main_3_clr_e));  // open: Qn, preset
  Bit_Extender #(.in_width(16), .out_width(12)) bit_extender_1 (.in(AR_output), .out(bit_extender_1_out));
  _8_BIT_main INPR (
    .CLK(clock_1_out), .CLR(1'b0), .LOAD(keyboard_1_avail), .INCR(1'b0), .INPUT(bit_extender_3_out),
    .OUTPUT(out_4));
  or or_1 (or_1_out, main_3_memory_write, and_1_out);
  DR_main DR (
    .CLK(clock_1_out), .CLR(1'b0), .LOAD(main_3_ld_dr), .INCR(main_3_incr_dr), .INPUT(multiplexer_1_out),
    .OUTPUT(DR_output), .DR(DR_dr));
  // AC_main AC: pin names not known; wires that end beside it: clock_1_out, main_3_clr_ac, main_3_ld_ac, main_3_incr_ac, main_4_out_ac, out_3, AC_p7, AC_p8
  _16_BIT_main IR (
    .CLK(clock_1_out), .CLR(1'b0), .LOAD(main_3_ld_ir), .INCR(1'b0), .INPUT(multiplexer_1_out),
    .OUTPUT(IR_output));
  _16_BIT_main TR (
    .CLK(clock_1_out), .CLR(1'b0), .LOAD(main_3_ld_tr), .INCR(1'b0), .INPUT(multiplexer_1_out),
    .OUTPUT(TR_output));
  _8_BIT_main main_5 (
    .CLK(clock_1_out), .CLR(or_2_out), .LOAD(main_3_ld_outr), .INCR(1'b0), .INPUT(multiplexer_1_out),
    .OUTPUT(out_5));
  RAM #(.addrWidth(12), .dataWidth(16), .bus("separate")) ram_1 (
    .addr(bit_extender_1_out), .din(multiplexer_1_out), .data(ram_1_data), .str(main_3_memory_write),
    .sel(or_1_out), .clk(clock_1_out), .ld(and_1_out), .clr(1'b0));
  _12_BIT_main AR (
    .CLK(clock_1_out), .CLR(main_3_clr_ar), .LOAD(main_3_ld_ar), .INCR(main_3_incr_ar),
    .INPUT(multiplexer_1_out), .OUTPUT(AR_output));
  _12_BIT_main PC (
    .CLK(clock_1_out), .CLR(main_3_clr_pc), .LOAD(main_3_ld_pc), .INCR(main_3_incr_pc),
    .INPUT(multiplexer_1_out), .OUTPUT(PC_output));
  J_K_Flip_Flop FGI (
    .J(keyboard_1_avail), .clk(clock_1_out), .K(main_3_fgi_reset), .Q(FGI_q));  // open: Qn, preset, en, reset
  J_K_Flip_Flop FGO (.J(or_2_out), .clk(clock_1_out), .K(main_3_fgo_reset), .Q(FGO_q));  // open: Qn, preset, en, reset
  Keyboard keyboard_1 (.clk(clock_1_out), .re(not_1_out), .clr(in_2), .avail(keyboard_1_avail), .data(keyboard_1_data));
  not not_1 (not_1_out, FGI_q);
  Bit_Extender #(.in_width(16), .out_width(7)) bit_extender_2 (.in(out_5), .out(bit_extender_2_out));
  J_K_Flip_Flop S (.J(in_1), .clk(clock_1_out), .K(main_3_reset_s), .Q(S_q));  // open: Qn, preset, en, reset
  or or_2 (or_2_out, bit_extender_2_out[6], bit_extender_2_out[5], bit_extender_2_out[4], bit_extender_2_out[3], bit_extender_2_out[2], bit_extender_2_out[1], bit_extender_2_out[0]);
  J_K_Flip_Flop IEN (
    .J(main_3_set_ien), .clk(clock_1_out), .K(main_3_reset_ien), .Q(IEN_q));  // open: Qn, preset, en, reset
  TTY tty_1 (.data(bit_extender_2_out), .clk(clock_1_out));  // open: we, clr
  assign bit_extender_3_out = {{9{1'b0}}, keyboard_1_data};  // Bit_Extender bit_extender_3
  Multiplexer #(.select(3), .width(16), .enable("false")) multiplexer_1 (
    .in1(AR_output), .in2(PC_output), .in3(DR_output), .in4(out_3), .in5(IR_output), .in6(TR_output),
    .in7(ram_1_data), .out(multiplexer_1_out), .sel(main_3_s0));  // open: in0
endmodule
