// Logisim project CONTROL UNIT.circ as structural Verilog: 1 circuit, main circuit main
module main (
  input  R,
  input  T0,
  input  T1,
  input  T2,
  input  T3,
  input  T4,
  input  I,
  input  IEN,
  input  B0,
  input  B1,
  input  B2,
  input  B3,
  input  B4,
  input  B5,
  input  B6,
  input  B7,
  input  B8,
  input  B9,
  input  B10,
  input  B11,
  input  T5,
  input  T6,
  input  D0,
  input  D1,
  input  D2,
  input  D3,
  input  D4,
  input  D5,
  input  D6,
  input  D7,
  output R_prime_T0,
  output R_prime_T1,
  output R_prime_T2,
  output RT0,
  output RT1,
  output RT2,
  output T_prime_0T_prime_1T_prime_2IENT_FGI_FGO,
  output D_prime_7IT3,
  output pB6,
  output pB7,
  output pB8,
  output pB9,
  output pB10,
  output pB11,
  output rB0,
  output rB1,
  output rB2,
  output rB3,
  output rB4,
  output rB5,
  output rB6,
  output rB7,
  output rB8,
  output rB9,
  output rB10,
  output rB11,
  output D0T4,
  output D1T4,
  output D2T4,
  output D3T4,
  output D4T4,
  output D5T4,
  output D6T4,
  output D0T5,
  output D1T5,
  output D2T5,
  output D5T5,
  output D6T5,
  output D6T6
);

  wire not_1_out, not_2_out, not_3_out, not_4_out, not_5_out, not_6_out;

  not not_1 (not_1_out, R);
  not not_2 (not_2_out, T1);
  not not_3 (not_3_out, T2);
  not not_4 (not_4_out, T0);
  not not_5 (not_5_out, I);
  not not_6 (not_6_out, D7);
  and and_1 (R_prime_T0, not_1_out, T0);
  and and_2 (R_prime_T1, not_1_out, T1);
  and and_3 (R_prime_T2, not_1_out, T2);
  and and_4 (RT0, T0, R);
  and and_5 (RT1, T1, R);
  and and_6 (RT2, T2, R);
  and and_7 (T_prime_0T_prime_1T_prime_2IENT_FGI_FGO, not_4_out, not_2_out, not_3_out, IEN);
  and and_8 (D_prime_7IT3, I, not_6_out, T3);
  and and_9 (pB6, I, B6, D7, T3);
  and and_10 (pB7, I, B7, D7, T3);
  and and_11 (pB8, I, B8, D7, T3);
  and and_12 (pB9, I, B9, D7, T3);
  and and_13 (pB10, I, B10, D7, T3);
  and and_14 (pB11, I, B11, D7, T3);
  and and_15 (rB0, not_5_out, B0, D7, T3);
  and and_16 (rB1, not_5_out, B1, D7, T3);
  and and_17 (rB2, not_5_out, B2, D7, T3);
  and and_18 (rB3, not_5_out, B3, D7, T3);
  and and_19 (rB4, not_5_out, B4, D7, T3);
  and and_20 (rB5, not_5_out, B5, D7, T3);
  and and_21 (rB6, not_5_out, B6, D7, T3);
  and and_22 (rB7, not_5_out, B7, D7, T3);
  and and_23 (rB8, not_5_out, B8, D7, T3);
  and and_24 (rB9, not_5_out, B9, D7, T3);
  and and_25 (rB10, not_5_out, B10, D7, T3);
  and and_26 (rB11, not_5_out, B11, D7, T3);
  and and_27 (D0T4, D0, T4);
  and and_28 (D1T4, D1, T4);
  and and_29 (D2T4, D2, T4);
  and and_30 (D3T4, D3, T4);
  and and_31 (D4T4, D4, T4);
  and and_32 (D5T4, D5, T4);
  and and_33 (D6T4, D6, T4);
  and and_34 (D0T5, D0, T5);
  and and_35 (D1T5, D1, T5);
  and and_36 (D2T5, D2, T5);
  and and_37 (D5T5, D5, T5);
  and and_38 (D6T5, D6, T5);
  and and_39 (D6T6, D6, T6);

  // Notes on the sheet:
  //   D_prime_7IT3: pull=down
endmodule
