// Logisim project CONTROL.circ as structural Verilog: 1 circuit, main circuit main
module main (
  input  AND,
  input  ADD,
  input  DDR,
  input  COM_AC,
  input  DINPR,
  input  SHR,
  input  SHL,
  input  COM_E,
  input  AC_15,
  input  DR_15,
  input  E,
  input  AC_14,
  input  DR_14,
  input  AC_13,
  input  DR_13,
  input  AC_12,
  input  DR_12,
  input  AC_11,
  input  DR_11,
  input  AC_10,
  input  DR_10,
  input  AC_9,
  input  DR_9,
  input  AC_8,
  input  DR_8,
  input  AC_7,
  input  DR_7,
  input  INPR_7,
  input  AC_6,
  input  DR_6,
  input  INPR_6,
  input  AC_5,
  input  DR_5,
  input  INPR_5,
  input  AC_4,
  input  DR_4,
  input  INPR_4,
  input  AC_3,
  input  DR_3,
  input  INPR_3,
  input  AC_2,
  input  DR_2,
  input  INPR_2,
  input  AC_1,
  input  DR_1,
  input  INPR_1,
  input  AC_0,
  input  DR_0,
  input  INPR_0,
  output E_2,
  output AC_15_2,
  output AC_14_2,
  output AC_13_2,
  output AC_12_2,
  output AC_11_2,
  output AC_10_2,
  output AC_9_2,
  output AC_8_2,
  output AC_7_2,
  output AC_6_2,
  output AC_5_2,
  output AC_4_2,
  output AC_3_2,
  output AC_2_2,
  output AC_1_2,
  output AC_0_2
);

  wire and_1_out, main_1_e_2, main_1_s, main_2_s, main_3_s, main_4_s, main_5_s, main_6_s, main_7_s, main_8_s,
       main_9_s, main_10_s, main_11_s, main_12_s, main_13_s, main_14_s, main_15_s, main_16_e_2, main_16_s,
       not_1_out;

  not not_1 (not_1_out, COM_E);
  and and_1 (and_1_out, not_1_out, E);
  ALU_15_BIT_main main_1 (
    .AND(AND), .AC(AC_15), .DR(DR_15), .ADD(ADD), .DDR(DDR), .COM(COM_AC), .SHR(SHR), .E(E), .SHL(SHL),
    .AC_N_1(AC_14), .S(main_1_s), .in_5(main_2_s), .AC_2(AC_15_2), .E_2(main_1_e_2));
  ALU_8_14_BIT_main main_2 (
    .AND(AND), .AC(AC_14), .DR(DR_14), .ADD(ADD), .DDR(DDR), .COM(COM_AC), .SHR(SHR), .AC_N(AC_15),
    .SHL(SHL), .AC_N_1(AC_13), .S(main_2_s), .in_5(main_3_s), .AC_2(AC_14_2));
  ALU_8_14_BIT_main main_3 (
    .AND(AND), .AC(AC_13), .DR(DR_13), .ADD(ADD), .DDR(DDR), .COM(COM_AC), .SHR(SHR), .AC_N(AC_14),
    .SHL(SHL), .AC_N_1(AC_12), .S(main_3_s), .in_5(main_4_s), .AC_2(AC_13_2));
  ALU_8_14_BIT_main main_4 (
    .AND(AND), .AC(AC_12), .DR(DR_12), .ADD(ADD), .DDR(DDR), .COM(COM_AC), .SHR(SHR), .AC_N(AC_13),
    .SHL(SHL), .AC_N_1(AC_11), .S(main_4_s), .in_5(main_5_s), .AC_2(AC_12_2));
  ALU_8_14_BIT_main main_5 (
    .AND(AND), .AC(AC_11), .DR(DR_11), .ADD(ADD), .DDR(DDR), .COM(COM_AC), .SHR(SHR), .AC_N(AC_12),
    .SHL(SHL), .AC_N_1(AC_10), .S(main_5_s), .in_5(main_6_s), .AC_2(AC_11_2));
  ALU_8_14_BIT_main main_6 (
    .AND(AND), .AC(AC_10), .DR(DR_10), .ADD(ADD), .DDR(DDR), .COM(COM_AC), .SHR(SHR), .AC_N(AC_11),
    .SHL(SHL), .AC_N_1(AC_9), .S(main_6_s), .in_5(main_7_s), .AC_2(AC_10_2));
  ALU_8_14_BIT_main main_7 (
    .AND(AND), .AC(AC_9), .DR(DR_9), .ADD(ADD), .DDR(DDR), .COM(COM_AC), .SHR(SHR), .AC_N(AC_10), .SHL(SHL),
    .AC_N_1(AC_8), .S(main_7_s), .in_5(main_8_s), .AC_2(AC_9_2));
  ALU_8_14_BIT_main main_8 (
    .AND(AND), .AC(AC_8), .DR(DR_8), .ADD(ADD), .DDR(DDR), .COM(COM_AC), .SHR(SHR), .AC_N(AC_9), .SHL(SHL),
    .AC_N_1(AC_7), .S(main_8_s), .in_5(main_9_s), .AC_2(AC_8_2));
  ALU_1_BIT_main main_9 (
    .AND(AND), .AC(AC_7), .DR(DR_7), .ADD(ADD), .DDR(DDR), .DINPR(DINPR), .INPR(INPR_7), .COM(COM_AC),
    .SHR(SHR), .AC_N(AC_8), .SHL(SHL), .AC_N_1(AC_6), .S(main_9_s), .in_5(main_10_s), .AC_2(AC_7_2));
  ALU_1_BIT_main main_10 (
    .AND(AND), .AC(AC_6), .DR(DR_6), .ADD(ADD), .DDR(DDR), .DINPR(DINPR), .INPR(INPR_6), .COM(COM_AC),
    .SHR(SHR), .AC_N(AC_7), .SHL(SHL), .AC_N_1(AC_5), .S(main_10_s), .in_5(main_11_s), .AC_2(AC_6_2));
  ALU_1_BIT_main main_11 (
    .AND(AND), .AC(AC_5), .DR(DR_5), .ADD(ADD), .DDR(DDR), .DINPR(DINPR), .INPR(INPR_5), .COM(COM_AC),
    .SHR(SHR), .AC_N(AC_6), .SHL(SHL), .AC_N_1(AC_4), .S(main_11_s), .in_5(main_12_s), .AC_2(AC_5_2));
  ALU_1_BIT_main main_12 (
    .AND(AND), .AC(AC_4), .DR(DR_4), .ADD(ADD), .DDR(DDR), .DINPR(DINPR), .INPR(INPR_4), .COM(COM_AC),
    .SHR(SHR), .AC_N(AC_5), .SHL(SHL), .AC_N_1(AC_3), .S(main_12_s), .in_5(main_13_s), .AC_2(AC_4_2));
  ALU_1_BIT_main main_13 (
    .AND(AND), .AC(AC_3), .DR(DR_3), .ADD(ADD), .DDR(DDR), .DINPR(DINPR), .INPR(INPR_3), .COM(COM_AC),
    .SHR(SHR), .AC_N(AC_4), .SHL(SHL), .AC_N_1(AC_2), .S(main_13_s), .in_5(main_14_s), .AC_2(AC_3_2));
  ALU_1_BIT_main main_14 (
    .AND(AND), .AC(AC_2), .DR(DR_2), .ADD(ADD), .DDR(DDR), .DINPR(DINPR), .INPR(INPR_2), .COM(COM_AC),
    .SHR(SHR), .AC_N(AC_3), .SHL(SHL), .AC_N_1(AC_1), .S(main_14_s), .in_5(main_15_s), .AC_2(AC_2_2));
  ALU_1_BIT_main main_15 (
    .AND(AND), .AC(AC_1), .DR(DR_1), .ADD(ADD), .DDR(DDR), .DINPR(DINPR), .INPR(INPR_1), .COM(COM_AC),
    .SHR(SHR), .AC_N(AC_2), .SHL(SHL), .AC_N_1(AC_0), .S(main_15_s), .in_5(main_16_s), .AC_2(AC_1_2));
  ALU_0_BIT_main main_16 (
    .AND(AND), .AC(AC_0), .DR(DR_0), .ADD(ADD), .DDR(DDR), .DINPR(DINPR), .INPR(INPR_0), .COM(COM_AC),
    .SHR(SHR), .AC_N(AC_1), .SHL(SHL), .E(E), .S(main_16_s), .AC_2(AC_0_2), .E_2(main_16_e_2));
  or or_1 (E_2, and_1_out, main_16_e_2, main_1_s, main_1_e_2);
endmodule
