// Logisim project COUNTER.circ as structural Verilog: 1 circuit, main circuit main
// A16
module main (
  input  CLK,
  input  Clear,
  input  Load,
  output [3:0] A1
);

  wire and_1_out, and_2_out, and_3_out, and_4_out, and_5_out, and_6_out, and_7_out, and_8_out, and_9_out,
       and_10_out, and_11_out, and_12_out, and_13_out, not_1_out, not_2_out, not_3_out, not_4_out, not_5_out,
       not_6_out, or_1_out, or_2_out, or_3_out, or_4_out, or_5_out, or_6_out, or_7_out, or_8_out;

  not not_1 (not_1_out, Clear);
  not not_2 (not_2_out, Load);
  not not_3 (not_3_out, 1'b0);
  not not_4 (not_4_out, 1'b0);
  not not_5 (not_5_out, 1'b0);
  not not_6 (not_6_out, 1'b0);
  and and_1 (and_1_out, not_1_out, not_2_out);
  and and_2 (and_2_out, not_1_out, Load);
  and and_3 (and_3_out, and_1_out, 1'b0);
  and and_4 (and_4_out, and_1_out, not_3_out);
  and and_5 (and_5_out, and_2_out, A1[0]);
  and and_6 (and_6_out, and_1_out, 1'b0);
  and and_7 (and_7_out, and_1_out, not_4_out);
  and and_8 (and_8_out, and_1_out, 1'b0);
  and and_9 (and_9_out, and_1_out, not_5_out);
  and and_10 (and_10_out, and_1_out, 1'b0);
  and and_11 (and_11_out, and_1_out, not_6_out);
  and and_12 (and_12_out, and_5_out, A1[1]);
  and and_13 (and_13_out, and_12_out, A1[2]);
  or or_1 (or_1_out, and_2_out, and_3_out);
  or or_2 (or_2_out, Clear, and_2_out, and_4_out);
  or or_3 (or_3_out, and_5_out, and_6_out);
  or or_4 (or_4_out, Clear, and_5_out, and_7_out);
  or or_5 (or_5_out, and_12_out, and_8_out);
  or or_6 (or_6_out, Clear, and_12_out, and_9_out);
  or or_7 (or_7_out, and_13_out, and_10_out);
  or or_8 (or_8_out, Clear, and_13_out, and_11_out);
  J_K_Flip_Flop j_k_ff_1 (.J(or_1_out), .clk(CLK), .K(or_2_out), .Q(A1[0]));  // open: Qn, preset, en, reset
  J_K_Flip_Flop j_k_ff_2 (.J(or_3_out), .clk(CLK), .K(or_4_out), .Q(A1[1]));  // open: Qn, preset, en, reset
  J_K_Flip_Flop j_k_ff_3 (.J(or_5_out), .clk(CLK), .K(or_6_out), .Q(A1[2]));  // open: Qn, preset, en, reset
  J_K_Flip_Flop j_k_ff_4 (.J(or_7_out), .clk(CLK), .K(or_8_out), .Q(A1[3]));  // open: Qn, preset, en, reset
endmodule
