// Logisim project CU.circ as structural Verilog: 1 circuit, main circuit main
module main (
  input  R,
  input  [6:0] TIME,
  input  [7:0] DECODED__BIT,
  input  IEN,
  input  [11:0] IR_0_11,
  input  I,
  input  DR,
  input  FGO,
  input  FGI,
  input  E,
  input  AC,
  input  AC_15,
  output S0,
  output S1,
  output S2,
  output COM_E,
  output AND,
  output ADD,
  output DDR,
  output DINPR,
  output COM_AC,
  output SHR,
  output SHL,
  output SET_R,
  output LD_AR,
  output LOAD_I,
  output LD_PC,
  output SET_IEN,
  output LD_DR,
  output LD_AC,
  output LD_E,
  output LD_IR,
  output LD_TR,
  output LD_OUTR,
  output CLR_AR,
  output CLR_E,
  output CLR_PC,
  output CLR_AC,
  output RESET_IEN,
  output RESET_R,
  output SC_RESET,
  output INCR_AR,
  output FGI_RESET,
  output INCR_PC,
  output INCR_DR,
  output INCR_AC,
  output MEMORY_WRITE,
  output RESET_S,
  output FGO_RESET
);

  wire and_1_out, and_2_out, and_3_out, and_4_out, and_5_out, and_6_out, and_7_out, main_1_d0t4, main_1_d1t4,
       main_1_d2t4, main_1_d3t4, main_1_d4t4, main_1_d5t5, main_1_d6t4, main_1_d6t6, main_1_d_prime_7it3,
       main_1_pb6, main_1_pb8, main_1_pb9, main_1_r_prime_t0, main_1_rb1, main_1_rb2, main_1_rb3, main_1_rb4,
       not_1_out, not_2_out, not_3_out, not_4_out;

  not not_1 (not_1_out, DR);
  not not_2 (not_2_out, E);
  not not_3 (not_3_out, AC);
  not not_4 (not_4_out, AC_15);
  and and_1 (and_1_out, not_1_out, main_1_d6t6);
  CONTROL_UNIT_main main_1 (
    .R(R), .T0(TIME[0]), .T1(TIME[1]), .T2(TIME[2]), .T3(TIME[3]), .T4(TIME[4]), .T5(TIME[5]), .T6(TIME[6]),
    .D0(DECODED__BIT[0]), .D1(DECODED__BIT[1]), .D2(DECODED__BIT[2]), .D3(DECODED__BIT[3]),
    .D4(DECODED__BIT[4]), .D5(DECODED__BIT[5]), .D6(DECODED__BIT[6]), .D7(DECODED__BIT[7]), .IEN(IEN),
    .B0(IR_0_11[0]), .B1(IR_0_11[1]), .B2(IR_0_11[2]), .B3(IR_0_11[3]), .B4(IR_0_11[4]), .B5(IR_0_11[5]),
    .B6(IR_0_11[6]), .B7(IR_0_11[7]), .B8(IR_0_11[8]), .B9(IR_0_11[9]), .B10(IR_0_11[10]), .B11(IR_0_11[11]),
    .I(I), .R_prime_T0(main_1_r_prime_t0), .R_prime_T1(LD_IR), .R_prime_T2(LOAD_I), .RT0(CLR_AR),
    .RT1(CLR_PC), .RT2(RESET_R), .T_prime_0T_prime_1T_prime_2IENT_FGI_FGO(SET_R),
    .D_prime_7IT3(main_1_d_prime_7it3), .pB6(main_1_pb6), .pB7(SET_IEN), .pB8(main_1_pb8), .pB9(main_1_pb9),
    .pB10(FGO_RESET), .pB11(DINPR), .rB0(RESET_S), .rB1(main_1_rb1), .rB2(main_1_rb2), .rB3(main_1_rb3),
    .rB4(main_1_rb4), .rB5(INCR_AC), .rB6(SHL), .rB7(SHR), .rB8(COM_E), .rB9(COM_AC), .rB10(CLR_E),
    .rB11(CLR_AC), .D0T4(main_1_d0t4), .D1T4(main_1_d1t4), .D2T4(main_1_d2t4), .D3T4(main_1_d3t4),
    .D4T4(main_1_d4t4), .D5T4(INCR_AR), .D6T4(main_1_d6t4), .D0T5(AND), .D1T5(ADD), .D2T5(DDR),
    .D5T5(main_1_d5t5), .D6T5(INCR_DR), .D6T6(main_1_d6t6));
  and and_2 (and_2_out, AC_15, main_1_rb3);
  and and_3 (and_3_out, not_4_out, main_1_rb4);
  and and_4 (and_4_out, main_1_pb9, FGI);
  and and_5 (and_5_out, main_1_rb1, not_2_out);
  and and_6 (and_6_out, main_1_rb2, not_3_out);
  and and_7 (and_7_out, main_1_pb8, FGO);
  or or_1 (S0, main_1_d4t4, main_1_d5t5, DDR, LD_IR, LOAD_I, main_1_d6t6, main_1_d_prime_7it3, main_1_d0t4, main_1_d1t4, main_1_d2t4, main_1_d6t4);
  or or_2 (S1, DDR, main_1_d6t4, LD_IR, main_1_d0t4, main_1_d1t4, main_1_d2t4, main_1_d6t6, main_1_r_prime_t0, CLR_AR, main_1_d_prime_7it3, CLR_PC, INCR_AR);
  or or_3 (S2, LOAD_I, main_1_d0t4, main_1_d2t4, main_1_d1t4, main_1_d3t4, LD_IR, main_1_d_prime_7it3, main_1_d6t4, CLR_PC, FGO_RESET);
  or or_4 (LD_AR, main_1_r_prime_t0, LOAD_I, main_1_d_prime_7it3);
  or or_5 (LD_PC, main_1_d4t4, main_1_d5t5);
  or or_6 (LD_DR, main_1_d0t4, main_1_d1t4, main_1_d2t4, main_1_d6t4);
  or or_7 (LD_AC, SHL, SHR, COM_AC, DINPR, AND, ADD, DDR);
  or or_8 (LD_E, ADD, SHR, SHL);
  or or_9 (SC_RESET, RESET_R, main_1_d3t4, main_1_d4t4, AND, ADD, DDR, main_1_d5t5, main_1_d6t6, main_1_pb6, SET_IEN, main_1_pb8, main_1_pb9, FGO_RESET, DINPR, RESET_S, main_1_rb1, main_1_rb2, main_1_rb3, main_1_rb4, INCR_AC, SHL, SHR, COM_E, COM_AC, CLR_E, CLR_AC);
  or or_10 (MEMORY_WRITE, main_1_d3t4, CLR_PC, INCR_AR, main_1_d6t6);
  or or_11 (RESET_IEN, main_1_pb6, RESET_R);
  or or_12 (INCR_PC, LD_IR, RESET_R, and_7_out, and_4_out, and_5_out, and_6_out, and_2_out, and_3_out, and_1_out);

  assign FGI_RESET = DINPR;
  assign LD_OUTR = FGO_RESET;
  assign LD_TR = CLR_AR;
endmodule
