// Logisim project DR.circ as structural Verilog: 1 circuit, main circuit main
module main (
  input  CLK,
  input  CLR,
  input  LOAD,
  input  INCR,
  input  [15:0] INPUT,
  output [15:0] OUTPUT,
  output DR
);

  // _16_BIT_register___Copy_main main_1: pin names not known; wires that end beside it: CLK, CLR, LOAD, INCR, OUTPUT[0], OUTPUT[1], OUTPUT[2], OUTPUT[3], OUTPUT[4], OUTPUT[5], OUTPUT[6], OUTPUT[7], OUTPUT[8], OUTPUT[9], OUTPUT[10], OUTPUT[11], OUTPUT[12], OUTPUT[13], OUTPUT[14], OUTPUT[15]
  or or_1 (DR, OUTPUT[0], OUTPUT[1], OUTPUT[2], OUTPUT[3], OUTPUT[4], OUTPUT[5], OUTPUT[6], OUTPUT[7], OUTPUT[9], OUTPUT[10], OUTPUT[11], OUTPUT[12], OUTPUT[13], OUTPUT[14], OUTPUT[15], OUTPUT[8]);
endmodule
