// Logisim project IR CONTROL.circ as structural Verilog: 1 circuit, main circuit main
module main (
  input  [15:0] IR_INPUT,
  output [11:0] IR_0_11,
  output [7:0] OUTPUT,
  output I
);

  Decoder #(.select(3), .enable("false")) decoder_1 (
    .out0(OUTPUT[0]), .out1(OUTPUT[1]), .out2(OUTPUT[2]), .out3(OUTPUT[3]), .out4(OUTPUT[4]),
    .out5(OUTPUT[5]), .out6(OUTPUT[6]), .out7(OUTPUT[7]), .sel(IR_INPUT[14:12]));

  assign I = IR_INPUT[15];
  assign IR_0_11 = IR_INPUT[11:0];
endmodule
